# Fritzing sketch Main electrical diagram (saved by Fritzing 0.9.3b)
breadboards: 1

parts:
  5V_USB_Supply = 4 x AAA Battery Mount
  12V_Main_Battery = 4 x AAA Battery Mount
  Right_Motor_Controller = L298 [package=multiwatt15]
  part = Arduino Uno (Rev3) - ICSP
  Left_Motor_Controller = L298 [package=multiwatt15]
  Left_Motor = DC Motor
  Right_Motor = DC Motor
  part_2 = Raspberry Pi 3 [part_number=RPI-3-V1.2]
  Raspberry_Pi_camera = 640x480 CMOS Color Camera [package=camera_cmos_con]
  Pan_Servo = Basic Servo
  Tilt_Servo = Basic Servo
  Power_switch = Square Pushbutton

nets:
  GND: 5V_USB_Supply.-, 12V_Main_Battery.-, Right_Motor_Controller.GND, part.GND, part_2.GND, Pan_Servo.gnd, Tilt_Servo.gnd
  5V: 5V_USB_Supply.+, Right_Motor_Controller.VLS, part.5V, Left_Motor_Controller.VLS, part_2.5V, Pan_Servo.vcc, Tilt_Servo.vcc
  N1: Right_Motor_Controller.OUT1, Right_Motor_Controller.OUT2, Right_Motor.pin_1
  N2: Right_Motor_Controller.VS, Left_Motor_Controller.VS, Power_switch.leg1
  N3: Right_Motor_Controller.IN1, Right_Motor_Controller.IN2, part.D9_PWM
  N4: Right_Motor_Controller.ENA, Right_Motor_Controller.ENB, part.D10_PWM/SS
  N5: Right_Motor_Controller.IN3, Right_Motor_Controller.IN4, part.D8
  N6: Right_Motor_Controller.OUT3, Right_Motor_Controller.OUT4, Right_Motor.pin_2
  N7: part.ICSP_MISO, part.D12/MISO, Pan_Servo.pulse
  N8: part.ICSP_MOSI, Tilt_Servo.pulse
  N9: part.D0/RX, part_2.GIPO21
  N10: part.D1/TX, part_2.GIPO20
  N11: part.D4, Left_Motor_Controller.IN3, Left_Motor_Controller.IN4
  N12: part.D5_PWM, Left_Motor_Controller.IN1, Left_Motor_Controller.IN2
  N13: part.D6_PWM, Left_Motor_Controller.ENA, Left_Motor_Controller.ENB
  N14: Left_Motor_Controller.OUT1, Left_Motor_Controller.OUT2, Left_Motor.pin_1
  N15: Left_Motor_Controller.OUT3, Left_Motor_Controller.OUT4, Left_Motor.pin_2
  N16: part_2.GPIO2, Raspberry_Pi_camera.Y6

notes:
  USB Link
  Bundled raspi camera cable
